// Logisim project Alarm_LED.circ as structural Verilog: 1 circuit, main circuit display
module display (
  input  Mode,
  input  RST,
  input  DecSecs,
  input  IncSecs,
  input  RSTalarm,
  input  up1,
  input  RSTarrows,
  input  Left,
  input  down1,
  input  Right,
  output G0,
  output F0,
  output out_13,
  output A0,
  output B0,
  output DP0,
  output C0,
  output E0,
  output D0,
  output A1,
  output F1,
  output G1,
  output B1,
  output GA1,
  output FA1,
  output G2,
  output D1,
  output C1,
  output E1,
  output AA1,
  output F2,
  output BA1,
  output A2,
  output B2,
  output CA1,
  output DA1,
  output C2,
  output D2,
  output EA1,
  output E2,
  output GA2,
  output FA2,
  output G3,
  output F3,
  output AA2,
  output BA2,
  output A3,
  output B3,
  output CA2,
  output DA2,
  output C3,
  output D3,
  output EA2,
  output E3,
  output FA3,
  output AA3,
  output F4,
  output A4,
  output GA3,
  output G4,
  output BA3,
  output B4,
  output CA3,
  output EA3,
  output C4,
  output DA3,
  output E4,
  output D4,
  output FA4,
  output F5,
  output AA4,
  output A5,
  output BA4,
  output B5,
  output GA4,
  output CA4,
  output G5,
  output C5,
  output DA4,
  output D5,
  output EA4,
  output E5
);

  wire and_2_out, and_3_out, and_4_out, and_5_out, and_6_out, and_7_out, and_8_out, and_9_out, and_10_out,
       and_11_out, and_12_out, and_13_out, and_14_out, and_15_out, and_17_out, and_18_out, and_19_out,
       and_20_out, and_21_out, and_22_out, and_23_out, and_24_out, and_25_out, and_26_out, and_27_out,
       and_28_out, and_32_out, clock_1_out, decoder_1_out0, decoder_1_out1, decoder_1_out2, decoder_1_out3,
       multiplexer_1_out, multiplexer_2_out, multiplexer_3_out, multiplexer_5_out, multiplexer_6_out,
       multiplexer_7_out, multiplexer_13_out, multiplexer_15_out, multiplexer_16_out, multiplexer_17_out,
       multiplexer_18_out, multiplexer_19_out, multiplexer_20_out, multiplexer_21_out, multiplexer_22_out,
       multiplexer_23_out, multiplexer_24_out, multiplexer_25_out, multiplexer_27_out, multiplexer_28_out,
       multiplexer_31_out, multiplexer_33_out, multiplexer_35_out, multiplexer_36_out, multiplexer_37_out,
       multiplexer_38_out, multiplexer_39_out, multiplexer_41_out, multiplexer_42_out, multiplexer_43_out,
       multiplexer_44_out, multiplexer_45_out, nor_1_out, nor_2_out, nor_3_out, nor_4_out, nor_5_out,
       nor_6_out, nor_8_out, nor_9_out, nor_10_out, nor_11_out, nor_12_out, not_1_out, not_2_out, not_3_out,
       not_4_out, not_5_out, not_6_out, not_7_out, not_8_out, not_9_out, not_10_out, not_11_out, not_12_out,
       not_13_out, not_14_out, not_15_out, not_16_out, not_17_out, or_1_out, or_2_out, or_3_out, or_4_out,
       or_5_out, or_6_out, or_7_out, or_8_out, or_9_out, or_10_out, or_11_out, subtractor_1_bout,
       subtractor_2_bout, subtractor_3_bout, subtractor_4_bout, t_ff_1_q, undriven;
  wire [1:0] counter_11_q, multiplexer_40_out;
  wire [2:0] counter_2_q, counter_6_q, counter_7_q, counter_9_q, multiplexer_10_out, multiplexer_12_out,
       multiplexer_14_out, multiplexer_30_out, multiplexer_34_out;
  wire [3:0] counter_1_q, counter_3_q, counter_4_q, counter_5_q, counter_8_q, counter_10_q,
       multiplexer_4_out, multiplexer_8_out, multiplexer_9_out, multiplexer_11_out, multiplexer_26_out,
       multiplexer_29_out, multiplexer_32_out, nor_7_out, subtractor_1_out, subtractor_2_out,
       subtractor_3_out, subtractor_4_out;

  Clock clock_1 (.out(clock_1_out));
  and and_1 (DP0, clock_1_out, not_10_out);
  Multiplexer multiplexer_1 (.in0(IncSecs), .in1(not_1_out), .out(multiplexer_1_out), .sel(DecSecs));
  not not_1 (not_1_out, IncSecs);
  Multiplexer multiplexer_2 (.in0(up1), .in1(not_2_out), .out(multiplexer_2_out), .sel(down1));
  not not_2 (not_2_out, up1);
  Multiplexer multiplexer_3 (.in0(up1), .in1(not_3_out), .out(multiplexer_3_out), .sel(down1));
  not not_3 (not_3_out, up1);
  Multiplexer #(.width(4)) multiplexer_4 (.in0(4'b1001), .in1(4'b0011), .out(multiplexer_4_out), .sel(nor_2_out));
  Multiplexer multiplexer_5 (.in0(multiplexer_1_out), .in1(clock_1_out), .out(multiplexer_5_out), .sel(not_10_out));
  Multiplexer multiplexer_6 (.in0(multiplexer_2_out), .in1(clock_1_out), .out(multiplexer_6_out), .sel(not_10_out));
  or or_1 (or_1_out, and_14_out, and_6_out, and_5_out);
  not not_4 (not_4_out, down1);
  Multiplexer multiplexer_7 (.in0(multiplexer_3_out), .in1(clock_1_out), .out(multiplexer_7_out), .sel(not_10_out));
  Multiplexer #(.width(4)) multiplexer_8 (.in0(4'b0000), .in1(multiplexer_4_out), .out(multiplexer_8_out), .sel(down1));
  or or_2 (or_2_out, or_1_out, multiplexer_17_out);
  not not_5 (not_5_out, not_7_out);
  Multiplexer #(.width(4)) multiplexer_9 (.in0(4'b0000), .in1(4'b1001), .out(multiplexer_9_out), .sel(down1));
  Counter #(.max('hf), .width(4)) counter_1 (
    .clr(RST), .load(or_2_out), .up(not_6_out), .count(multiplexer_15_out), .clk(multiplexer_18_out),
    .D(multiplexer_8_out), .Q(counter_1_q));  // open: carry
  not not_6 (not_6_out, down1);
  Counter #(.max('h7), .width(3)) counter_2 (
    .clr(RST), .load(or_1_out), .up(not_6_out), .count(or_2_out), .clk(multiplexer_18_out),
    .D(multiplexer_10_out), .Q(counter_2_q));  // open: carry
  Multiplexer #(.width(3)) multiplexer_10 (.in0(3'b000), .in1(3'b010), .out(multiplexer_10_out), .sel(and_6_out));
  Counter #(.max('hf), .width(4)) counter_3 (
    .clr(RST), .load(multiplexer_16_out), .up(not_7_out), .count(1'b1), .clk(multiplexer_5_out),
    .D(multiplexer_11_out), .Q(counter_3_q));  // open: carry
  not not_7 (not_7_out, DecSecs);
  Multiplexer #(.width(4)) multiplexer_11 (.in0(4'b0000), .in1(4'b1001), .out(multiplexer_11_out), .sel(DecSecs));
  Counter #(.max('hf), .width(4)) counter_4 (
    .clr(RST), .load(or_5_out), .up(not_7_out), .count(multiplexer_16_out), .clk(multiplexer_5_out),
    .D({1'b0, multiplexer_12_out}), .Q(counter_4_q));  // open: carry
  Multiplexer #(.width(3)) multiplexer_12 (.in0(3'b000), .in1(3'b101), .out(multiplexer_12_out), .sel(not_5_out));
  Multiplexer multiplexer_13 (.in0(and_11_out), .in1(and_11_out), .out(multiplexer_13_out), .sel(not_10_out));
  Counter #(.max('hf), .width(4)) counter_5 (
    .clr(RST), .load(multiplexer_19_out), .up(not_4_out), .count(multiplexer_13_out),
    .clk(multiplexer_23_out), .D(multiplexer_9_out), .Q(counter_5_q));  // open: carry
  Counter #(.max('h7), .width(3)) counter_6 (
    .clr(RST), .load(or_3_out), .up(not_4_out), .count(multiplexer_19_out), .clk(multiplexer_23_out),
    .D(multiplexer_14_out), .Q(counter_6_q));  // open: carry
  Multiplexer #(.width(3)) multiplexer_14 (.in0(3'b000), .in1(3'b101), .out(multiplexer_14_out), .sel(not_8_out));
  not not_8 (not_8_out, not_4_out);
  or or_3 (or_3_out, and_8_out, and_4_out);
  Multiplexer multiplexer_15 (.in1(and_8_out), .out(multiplexer_15_out), .sel(not_10_out));  // open: in0
  or or_4 (or_4_out, decoder_1_out1, decoder_1_out3, decoder_1_out2);
  Multiplexer multiplexer_16 (.in0(and_10_out), .in1(nor_5_out), .out(multiplexer_16_out), .sel(DecSecs));
  or or_5 (or_5_out, and_11_out, and_3_out);
  Multiplexer multiplexer_17 (.in0(and_9_out), .in1(nor_1_out), .out(multiplexer_17_out), .sel(down1));
  Multiplexer multiplexer_18 (.in0(multiplexer_7_out), .in1(1'b0), .out(multiplexer_18_out), .sel(and_2_out));
  and and_2 (and_2_out, or_4_out, t_ff_1_q);
  and and_3 (and_3_out, DecSecs, nor_5_out, nor_6_out);
  Multiplexer multiplexer_19 (.in0(and_7_out), .in1(nor_3_out), .out(multiplexer_19_out), .sel(down1));
  and and_4 (and_4_out, down1, nor_4_out, nor_3_out);
  and and_5 (and_5_out, counter_2_q[0], and_9_out, counter_2_q[2]);
  and and_6 (and_6_out, nor_2_out, down1, nor_1_out);
  and and_7 (and_7_out, counter_5_q[3], multiplexer_21_out, counter_5_q[0]);
  and and_8 (and_8_out, counter_6_q[0], and_7_out, counter_6_q[2]);
  Multiplexer multiplexer_20 (.in0(1'b1), .in1(and_8_out), .out(multiplexer_20_out), .sel(not_10_out));
  and and_9 (and_9_out, counter_1_q[3], multiplexer_20_out, counter_1_q[0]);
  nor nor_1 (nor_1_out, counter_1_q[0], counter_1_q[1], counter_1_q[2], counter_1_q[3]);
  nor nor_2 (nor_2_out, counter_2_q[0], counter_2_q[2], counter_2_q[1]);
  and and_10 (and_10_out, counter_3_q[3], counter_3_q[0]);
  and and_11 (and_11_out, counter_4_q[0], and_10_out, counter_4_q[2]);
  Multiplexer multiplexer_21 (.in0(1'b1), .in1(and_11_out), .out(multiplexer_21_out), .sel(not_10_out));
  nor nor_3 (nor_3_out, counter_5_q[3], counter_5_q[2], counter_5_q[1], counter_5_q[0]);
  nor nor_4 (nor_4_out, counter_6_q[0], counter_6_q[1], counter_6_q[2]);
  not not_9 (not_9_out, Mode);
  nor nor_5 (nor_5_out, counter_3_q[3], counter_3_q[2], counter_3_q[1], counter_3_q[0]);
  nor nor_6 (nor_6_out, counter_4_q[0], counter_4_q[2], counter_4_q[1]);
  and and_12 (and_12_out, multiplexer_20_out, counter_1_q[0], counter_1_q[1]);
  and and_13 (and_13_out, and_12_out, counter_2_q[1]);
  and and_14 (and_14_out, and_13_out, multiplexer_22_out);
  T_Flip_Flop t_ff_1 (.T(not_9_out), .clk(not_9_out), .Q(t_ff_1_q));  // open: Qn, reset, preset
  Multiplexer multiplexer_22 (.in0(up1), .in1(1'b1), .out(multiplexer_22_out), .sel(not_10_out));
  not not_10 (not_10_out, t_ff_1_q);
  // BCD_to_7_Segment_decoder bcd_to_7_segment_decoder_1: pin names not known; wires that end beside it: G2, E2, F2, D2, counter_5_q, A2, C2, B2
  // BCD_to_7_Segment_decoder bcd_to_7_segment_decoder_2: pin names not known; wires that end beside it: G0, E0, F0, D0, counter_3_q, A0, C0
  // BCD_to_7_Segment_decoder bcd_to_7_segment_decoder_3: pin names not known; wires that end beside it: G3, E3, F3, D3, {1'b0, counter_6_q}, A3, C3, B3
  // BCD_to_7_Segment_decoder bcd_to_7_segment_decoder_4: pin names not known; wires that end beside it: G4, E4, F4, D4, counter_1_q, A4, C4, B4
  or or_6 (or_6_out, decoder_1_out0, decoder_1_out3, decoder_1_out2);
  Multiplexer multiplexer_23 (.in0(multiplexer_6_out), .in1(1'b0), .out(multiplexer_23_out), .sel(and_15_out));
  and and_15 (and_15_out, or_6_out, t_ff_1_q);
  // BCD_to_7_Segment_decoder bcd_to_7_segment_decoder_5: pin names not known; wires that end beside it: G1, E1, F1, D1, {1'b0, counter_4_q[2:0]}, A1, C1, B1
  _7_Segment_Display u_7_segment_display_1 (.g(G5), .f(F5), .a(A5), .b(B5), .e(E5), .d(D5), .c(C5));  // open: dp
  _7_Segment_Display u_7_segment_display_2 (.g(G4), .f(F4), .a(A4), .b(B4), .e(E4), .d(D4), .c(C4));  // open: dp
  // BCD_to_7_Segment_decoder bcd_to_7_segment_decoder_6: pin names not known; wires that end beside it: G5, E5, F5, D5, {1'b0, counter_2_q}, A5, C5, B5
  _7_Segment_Display u_7_segment_display_3 (.g(G3), .f(F3), .a(A3), .b(B3), .e(E3), .d(D3), .c(C3));  // open: dp
  Subtractor #(.width(4)) subtractor_1 (
    .a(counter_1_q), .b(counter_8_q), .out(subtractor_1_out), .bin(1'b0), .bout(subtractor_1_bout));
  _7_Segment_Display u_7_segment_display_4 (.g(G2), .f(F2), .a(A2), .b(B2), .e(E2), .d(D2), .c(C2));  // open: dp
  _7_Segment_Display u_7_segment_display_5 (.g(G1), .f(F1), .a(A1), .b(B1), .e(E1), .d(D1), .c(C1));  // open: dp
  Subtractor #(.width(4)) subtractor_2 (
    .a({1'b0, counter_2_q}), .b({1'b0, counter_9_q}), .out(subtractor_2_out), .bin(1'b0),
    .bout(subtractor_2_bout));
  _7_Segment_Display u_7_segment_display_6 (.g(G0), .f(F0), .a(A0), .b(B0), .e(E0), .d(D0), .c(C0));  // open: dp
  Subtractor #(.width(4)) subtractor_3 (
    .a(counter_5_q), .b(counter_10_q), .out(subtractor_3_out), .bin(1'b0), .bout(subtractor_3_bout));
  Subtractor #(.width(4)) subtractor_4 (
    .a({1'b0, counter_6_q}), .b({1'b0, counter_7_q}), .out(subtractor_4_out), .bin(1'b0),
    .bout(subtractor_4_bout));
  assign nor_7_out = ~(subtractor_3_out | subtractor_4_out | subtractor_1_out | subtractor_2_out);  // NOR_Gate nor_7, 4 bits wide
  Multiplexer multiplexer_24 (.in0(up1), .in1(not_11_out), .out(multiplexer_24_out), .sel(down1));
  not not_11 (not_11_out, up1);
  Multiplexer multiplexer_25 (.in0(up1), .in1(not_12_out), .out(multiplexer_25_out), .sel(down1));
  not not_12 (not_12_out, up1);
  Multiplexer #(.width(4)) multiplexer_26 (.in0(4'b1001), .in1(4'b0011), .out(multiplexer_26_out), .sel(nor_10_out));
  or or_7 (or_7_out, decoder_1_out0, decoder_1_out1, decoder_1_out3);
  Multiplexer multiplexer_27 (.in0(multiplexer_24_out), .in1(1'b0), .out(multiplexer_27_out), .sel(1'b0));
  and and_16 (out_13, clock_1_out, nor_7_out[0], nor_7_out[1], nor_7_out[2], nor_7_out[3]);
  Multiplexer multiplexer_28 (.in0(multiplexer_25_out), .in1(1'b0), .out(multiplexer_28_out), .sel(1'b0));
  or or_8 (or_8_out, and_26_out, and_21_out, and_20_out);
  and and_17 (and_17_out, or_7_out, t_ff_1_q);
  LED led_1 (.in(out_13));
  not not_13 (not_13_out, down1);
  not not_14 (not_14_out, down1);
  Multiplexer #(.width(4)) multiplexer_29 (
    .in0(4'b0000), .in1(multiplexer_26_out), .out(multiplexer_29_out), .sel(down1));
  or or_9 (or_9_out, or_8_out, multiplexer_35_out);
  Multiplexer #(.width(3)) multiplexer_30 (.in0(3'b000), .in1(3'b010), .out(multiplexer_30_out), .sel(and_21_out));
  Multiplexer multiplexer_31 (.in0(multiplexer_28_out), .in1(1'b0), .out(multiplexer_31_out), .sel(and_17_out));
  Multiplexer #(.width(4)) multiplexer_32 (.in0(4'b0000), .in1(4'b1001), .out(multiplexer_32_out), .sel(down1));
  Counter #(.max('h7), .width(3)) counter_7 (
    .clr(RSTalarm), .load(or_10_out), .up(not_13_out), .count(multiplexer_36_out), .clk(multiplexer_38_out),
    .D(multiplexer_34_out), .Q(counter_7_q));  // open: carry
  Multiplexer multiplexer_33 (.in0(undriven), .in1(and_19_out), .out(multiplexer_33_out), .sel(1'b0));
  Counter #(.max('hf), .width(4)) counter_8 (
    .clr(RSTalarm), .load(or_9_out), .up(not_14_out), .count(multiplexer_33_out), .clk(multiplexer_31_out),
    .D(multiplexer_29_out), .Q(counter_8_q));  // open: carry
  Counter #(.max('h7), .width(3)) counter_9 (
    .clr(RSTalarm), .load(or_8_out), .up(not_14_out), .count(or_9_out), .clk(multiplexer_31_out),
    .D(multiplexer_30_out), .Q(counter_9_q));  // open: carry
  Counter #(.max('hf), .width(4)) counter_10 (
    .clr(RSTalarm), .load(multiplexer_36_out), .up(not_13_out), .count(and_32_out), .clk(multiplexer_38_out),
    .D(multiplexer_32_out), .Q(counter_10_q));  // open: carry
  Multiplexer #(.width(3)) multiplexer_34 (.in0(3'b000), .in1(3'b101), .out(multiplexer_34_out), .sel(not_15_out));
  not not_15 (not_15_out, not_13_out);
  or or_10 (or_10_out, and_19_out, and_18_out);
  and and_18 (and_18_out, down1, nor_8_out, nor_11_out);
  Multiplexer multiplexer_35 (.in0(and_23_out), .in1(nor_9_out), .out(multiplexer_35_out), .sel(down1));
  Multiplexer multiplexer_36 (.in0(and_22_out), .in1(nor_11_out), .out(multiplexer_36_out), .sel(down1));
  and and_19 (and_19_out, counter_7_q[0], and_22_out, counter_7_q[2]);
  and and_20 (and_20_out, counter_9_q[0], and_23_out, counter_9_q[2]);
  and and_21 (and_21_out, nor_10_out, down1, nor_9_out);
  and and_22 (and_22_out, counter_10_q[3], 1'b1, counter_10_q[0]);
  nor nor_8 (nor_8_out, counter_7_q[0], counter_7_q[1], counter_7_q[2]);
  Multiplexer multiplexer_37 (.in0(1'b1), .in1(and_19_out), .out(multiplexer_37_out), .sel(1'b0));
  and and_23 (and_23_out, counter_8_q[3], multiplexer_37_out, counter_8_q[0]);
  nor nor_9 (nor_9_out, counter_8_q[0], counter_8_q[1], counter_8_q[2], counter_8_q[3]);
  nor nor_10 (nor_10_out, counter_9_q[0], counter_9_q[2], counter_9_q[1]);
  nor nor_11 (nor_11_out, counter_10_q[3], counter_10_q[2], counter_10_q[1], counter_10_q[0]);
  and and_24 (and_24_out, multiplexer_37_out, counter_8_q[0], counter_8_q[1]);
  and and_25 (and_25_out, and_24_out, counter_9_q[1]);
  or or_11 (or_11_out, decoder_1_out0, decoder_1_out1, decoder_1_out2);
  and and_26 (and_26_out, and_25_out, up1);
  // BCD_to_7_Segment_decoder bcd_to_7_segment_decoder_7: pin names not known; wires that end beside it: GA1, EA1, FA1, DA1, counter_10_q, AA1, CA1, BA1
  and and_27 (and_27_out, t_ff_1_q, or_11_out);
  // BCD_to_7_Segment_decoder bcd_to_7_segment_decoder_8: pin names not known; wires that end beside it: GA2, EA2, FA2, DA2, {1'b0, counter_7_q}, AA2, CA2, BA2
  Multiplexer multiplexer_38 (.in0(multiplexer_27_out), .in1(1'b0), .out(multiplexer_38_out), .sel(and_27_out));
  // BCD_to_7_Segment_decoder bcd_to_7_segment_decoder_9: pin names not known; wires that end beside it: GA3, EA3, FA3, DA3, counter_8_q, AA3, CA3, BA3
  _7_Segment_Display u_7_segment_display_7 (.g(GA4), .f(FA4), .a(AA4), .b(BA4), .e(EA4), .d(DA4), .c(CA4));  // open: dp
  _7_Segment_Display u_7_segment_display_8 (.g(GA3), .f(FA3), .a(AA3), .b(BA3), .e(EA3), .d(DA3), .c(CA3));  // open: dp
  // BCD_to_7_Segment_decoder bcd_to_7_segment_decoder_10: pin names not known; wires that end beside it: GA4, EA4, FA4, DA4, {1'b0, counter_9_q}, AA4, CA4, BA4
  _7_Segment_Display u_7_segment_display_9 (.g(GA2), .f(FA2), .a(AA2), .b(BA2), .e(EA2), .d(DA2), .c(CA2));  // open: dp
  _7_Segment_Display u_7_segment_display_10 (
    .g(GA1), .f(FA1), .a(AA1), .b(BA1), .e(EA1), .d(DA1), .c(CA1));  // open: dp
  Multiplexer multiplexer_39 (.in0(Right), .in1(not_17_out), .out(multiplexer_39_out), .sel(Left));
  not not_16 (not_16_out, Left);
  not not_17 (not_17_out, Right);
  Multiplexer #(.width(2)) multiplexer_40 (.in0(2'b00), .in1(2'b11), .out(multiplexer_40_out), .sel(Left));
  Multiplexer multiplexer_41 (.in0(and_28_out), .in1(nor_12_out), .out(multiplexer_41_out), .sel(Left));
  Counter #(.max('h3), .width(2)) counter_11 (
    .clr(RSTarrows), .load(multiplexer_41_out), .up(not_16_out), .count(t_ff_1_q), .clk(multiplexer_39_out),
    .D(multiplexer_40_out), .Q(counter_11_q));  // open: carry
  Decoder #(.select(2)) decoder_1 (
    .out0(decoder_1_out0), .out1(decoder_1_out1), .out2(decoder_1_out2), .out3(decoder_1_out3),
    .sel(counter_11_q), .en(1'b1));
  nor nor_12 (nor_12_out, counter_11_q[1], counter_11_q[0]);
  and and_28 (and_28_out, counter_11_q[1], counter_11_q[0]);
  Multiplexer multiplexer_42 (.in0(up1), .in1(decoder_1_out2), .out(multiplexer_42_out), .sel(down1));
  Multiplexer multiplexer_43 (.in0(up1), .in1(decoder_1_out0), .out(multiplexer_43_out), .sel(down1));
  and and_29 (multiplexer_33_out, multiplexer_42_out, decoder_1_out2);
  and and_30 (multiplexer_15_out, multiplexer_43_out, decoder_1_out0);
  Multiplexer multiplexer_44 (.in0(up1), .in1(decoder_1_out1), .out(multiplexer_44_out), .sel(down1));
  and and_31 (multiplexer_13_out, multiplexer_44_out, decoder_1_out1);
  Multiplexer multiplexer_45 (.in0(up1), .in1(decoder_1_out3), .out(multiplexer_45_out), .sel(down1));
  and and_32 (and_32_out, multiplexer_45_out, decoder_1_out3);
  // also tied to GND on the sheet: {subtractor_1_bout, subtractor_2_bout, subtractor_4_bout, subtractor_3_bout}
endmodule
