// Logisim project Caller.circ as structural Verilog: 1 circuit, main circuit main
module main (
);

  wire button_1_out, button_2_out, button_3_out, button_4_out, button_5_out, button_6_out, button_7_out,
       button_8_out, button_9_out, button_10_out, buzzer_1_p1, display_1_p6, display_1_p7, display_1_p8,
       display_1_p9, display_1_p10, display_1_p11, display_1_p12, display_1_p16, display_1_p17,
       display_1_p19, display_1_p20, display_1_p21, display_1_p22, display_1_p23, display_1_p24,
       display_1_p25, display_1_p26, display_1_p27, display_1_p28, display_1_p29, display_1_p30,
       display_1_p31, display_1_p33, display_1_p34, display_1_p35, display_1_p36, display_1_p37,
       display_1_p38, display_1_p39, display_1_p40, display_1_p41, display_1_p42, display_1_p43,
       display_1_p44, display_1_p45, display_1_p46, display_1_p47, display_1_p48, display_1_p49,
       display_1_p50, display_1_p51, display_1_p52, display_1_p53, display_1_p54, display_1_p55,
       display_1_p56, display_1_p57, display_1_p58, display_1_p59, display_1_p60, display_1_p61,
       display_1_p62, display_1_p63, display_1_p64, display_1_p65, display_1_p66, display_1_p67,
       display_1_p71, display_1_p72, display_1_p73, display_1_p74, display_1_p75, display_1_p76,
       display_1_p77, display_1_p78, display_1_p79, display_1_p80, display_1_p81, display_1_p82,
       display_1_p83, display_1_p84;

  Button button_1 (.out(button_1_out));
  Button button_2 (.out(button_2_out));
  Button button_3 (.out(button_3_out));
  Button button_4 (.out(button_4_out));
  _7_Segment_Display u_7_segment_display_1 (
    .g(display_1_p6), .f(display_1_p8), .a(display_1_p10), .b(display_1_p12), .e(display_1_p7),
    .d(display_1_p9), .c(display_1_p11));  // open: dp
  Button button_5 (.out(button_5_out));
  Button button_6 (.out(button_6_out));
  Button button_7 (.out(button_7_out));
  Button button_8 (.out(button_8_out));
  _7_Segment_Display u_7_segment_display_2 (
    .g(display_1_p16), .f(display_1_p19), .a(display_1_p23), .b(display_1_p27), .e(display_1_p17),
    .d(display_1_p20), .c(display_1_p24), .dp(display_1_p28));
  Button button_9 (.out(button_9_out));
  _7_Segment_Display u_7_segment_display_3 (
    .g(display_1_p21), .f(display_1_p25), .a(display_1_p29), .b(display_1_p31), .e(display_1_p22),
    .d(display_1_p26), .c(display_1_p30));  // open: dp
  Button button_10 (.out(button_10_out));
  _7_Segment_Display u_7_segment_display_4 (
    .g(display_1_p33), .f(display_1_p35), .a(display_1_p37), .b(display_1_p39), .e(display_1_p34),
    .d(display_1_p36), .c(display_1_p38));  // open: dp
  _7_Segment_Display u_7_segment_display_5 (
    .g(display_1_p40), .f(display_1_p42), .a(display_1_p44), .b(display_1_p46), .e(display_1_p41),
    .d(display_1_p43), .c(display_1_p45));  // open: dp
  _7_Segment_Display u_7_segment_display_6 (
    .g(display_1_p51), .f(display_1_p55), .a(display_1_p58), .b(display_1_p60), .e(display_1_p52),
    .d(display_1_p56), .c(display_1_p59));  // open: dp
  _7_Segment_Display u_7_segment_display_7 (
    .g(display_1_p47), .f(display_1_p49), .a(display_1_p53), .b(display_1_p57), .e(display_1_p48),
    .d(display_1_p50), .c(display_1_p54));  // open: dp
  _7_Segment_Display u_7_segment_display_8 (
    .g(display_1_p61), .f(display_1_p63), .a(display_1_p65), .b(display_1_p67), .e(display_1_p62),
    .d(display_1_p64), .c(display_1_p66));  // open: dp
  _7_Segment_Display u_7_segment_display_9 (
    .g(display_1_p71), .f(display_1_p73), .a(display_1_p75), .b(display_1_p77), .e(display_1_p72),
    .d(display_1_p74), .c(display_1_p76));  // open: dp
  LED led_1 (.in(buzzer_1_p1));
  // Buzzer buzzer_1: pin names not known; wires that end beside it: buzzer_1_p1
  // display display_1: pin names not known; wires that end beside it: button_1_out, button_2_out, button_3_out, button_5_out, button_4_out, display_1_p6, display_1_p7, display_1_p8, display_1_p9, display_1_p10, display_1_p11, display_1_p12, button_6_out, button_7_out, button_8_out, display_1_p16, display_1_p17, button_9_out, display_1_p19, display_1_p20, display_1_p21, display_1_p22, display_1_p23, display_1_p24, display_1_p25, display_1_p26, display_1_p27, display_1_p28, display_1_p29, display_1_p30, display_1_p31, button_10_out, display_1_p33, display_1_p34, display_1_p35, display_1_p36, display_1_p37, display_1_p38, display_1_p39, display_1_p40, display_1_p41, display_1_p42, display_1_p43, display_1_p44, display_1_p45, display_1_p46, display_1_p47, display_1_p48, display_1_p49, display_1_p50, display_1_p51, display_1_p52, display_1_p53, display_1_p54, display_1_p55, display_1_p56, display_1_p57, display_1_p58, display_1_p59, display_1_p60, display_1_p61, display_1_p62, display_1_p63, display_1_p64, display_1_p65, display_1_p66, display_1_p67, 14'h55, 7'b0010001, buzzer_1_p1, display_1_p71, display_1_p72, display_1_p73, display_1_p74, display_1_p75, display_1_p76, display_1_p77, display_1_p78, display_1_p79, display_1_p80, display_1_p81, display_1_p82, display_1_p83, display_1_p84
  _7_Segment_Display u_7_segment_display_10 (
    .g(display_1_p78), .f(display_1_p80), .a(display_1_p82), .b(display_1_p84), .e(display_1_p79),
    .d(display_1_p81), .c(display_1_p83));  // open: dp
endmodule
