// Logisim project DisplayDriver.circ as structural Verilog: 1 circuit, main circuit display
module display (
  input  RST,
  input  EN,
  output G0,
  output F0,
  output A0,
  output B0,
  output C0,
  output E0,
  output D0,
  output A1,
  output F1,
  output G1,
  output B1,
  output G2,
  output D1,
  output C1,
  output E1,
  output F2,
  output A2,
  output B2,
  output C2,
  output D2,
  output E2,
  output G3,
  output F3,
  output A3,
  output B3,
  output C3,
  output D3,
  output E3,
  output F4,
  output A4,
  output G4,
  output B4,
  output C4,
  output E4,
  output D4,
  output F5,
  output A5,
  output B5,
  output G5,
  output C5,
  output D5,
  output E5
);

  wire and_1_out, and_2_out, and_3_out, and_4_out, and_5_out, and_6_out, and_7_out, and_8_out, clock_1_out,
       d_ff_1_q, d_ff_1_qn, d_ff_2_q, d_ff_2_qn, d_ff_3_q, d_ff_3_qn, d_ff_4_q, d_ff_4_qn, d_ff_5_q,
       d_ff_5_qn, decoder_1_out0, decoder_1_out1, decoder_1_out2, decoder_1_out3, or_1_out, or_2_out;
  wire [1:0] counter_7_q;
  wire [2:0] counter_2_q, counter_4_q, counter_6_q;
  wire [3:0] bcd_to_7_segment_decoder_7_p1, bcd_to_7_segment_decoder_8_p1, bcd_to_7_segment_decoder_9_p2,
       bcd_to_7_segment_decoder_10_p1, counter_1_q, counter_3_q, counter_5_q;

  D_Flip_Flop d_ff_1 (.D(d_ff_1_qn), .clk(clock_1_out), .Q(d_ff_1_q), .Qn(d_ff_1_qn));  // open: preset, reset
  Clock clock_1 (.out(clock_1_out));
  D_Flip_Flop d_ff_2 (.D(d_ff_2_qn), .clk(d_ff_1_q), .Q(d_ff_2_q), .Qn(d_ff_2_qn));  // open: preset, reset
  or or_1 (or_1_out, and_8_out, and_1_out);
  D_Flip_Flop d_ff_3 (.D(d_ff_3_qn), .clk(d_ff_2_q), .Q(d_ff_3_q), .Qn(d_ff_3_qn));  // open: preset, reset
  or or_2 (or_2_out, or_1_out, and_4_out);
  Counter #(.max('hf), .width(4)) counter_1 (
    .clr(RST), .load(or_2_out), .count(and_3_out), .clk(d_ff_5_q), .D(4'b0000), .Q(counter_1_q));  // open: up, carry
  Counter #(.max('h7), .width(3)) counter_2 (
    .clr(RST), .load(or_1_out), .count(and_4_out), .clk(d_ff_5_q), .D(3'b000), .Q(counter_2_q));  // open: up, carry
  D_Flip_Flop d_ff_4 (.D(d_ff_4_qn), .clk(d_ff_3_q), .Q(d_ff_4_q), .Qn(d_ff_4_qn));  // open: preset, reset
  Counter #(.max('hf), .width(4)) counter_3 (
    .clr(RST), .load(and_5_out), .count(EN), .clk(d_ff_5_q), .D(4'b0000), .Q(counter_3_q));  // open: up, carry
  Counter #(.max('h7), .width(3)) counter_4 (
    .clr(RST), .load(and_6_out), .count(and_5_out), .clk(d_ff_5_q), .D(3'b000), .Q(counter_4_q));  // open: up, carry
  Counter #(.max('hf), .width(4)) counter_5 (
    .clr(RST), .load(and_2_out), .count(and_6_out), .clk(d_ff_5_q), .D(4'b0000), .Q(counter_5_q));  // open: up, carry
  Counter #(.max('h7), .width(3)) counter_6 (
    .clr(RST), .load(and_3_out), .count(and_2_out), .clk(d_ff_5_q), .D(3'b000), .Q(counter_6_q));  // open: up, carry
  D_Flip_Flop d_ff_5 (.D(d_ff_5_qn), .clk(d_ff_4_q), .Q(d_ff_5_q), .Qn(d_ff_5_qn));  // open: preset, reset
  and and_1 (and_1_out, counter_2_q[0], and_4_out, counter_2_q[2]);
  and and_2 (and_2_out, counter_5_q[3], and_6_out, counter_5_q[0]);
  and and_3 (and_3_out, counter_6_q[0], and_2_out, counter_6_q[2]);
  and and_4 (and_4_out, counter_1_q[3], and_3_out, counter_1_q[0]);
  and and_5 (and_5_out, counter_3_q[3], counter_3_q[0]);
  and and_6 (and_6_out, counter_4_q[0], and_5_out, counter_4_q[2]);
  and and_7 (and_7_out, and_3_out, counter_1_q[0], counter_1_q[1]);
  and and_8 (and_8_out, and_7_out, counter_2_q[1]);
  // BCD_to_7_Segment_decoder bcd_to_7_segment_decoder_1: pin names not known; wires that end beside it: G2, E2, F2, D2, counter_5_q, A2, C2, B2
  // BCD_to_7_Segment_decoder bcd_to_7_segment_decoder_2: pin names not known; wires that end beside it: G0, E0, F0, D0, counter_3_q, A0, C0
  // BCD_to_7_Segment_decoder bcd_to_7_segment_decoder_3: pin names not known; wires that end beside it: G3, E3, F3, D3, {1'b0, counter_6_q}, A3, C3, B3
  // BCD_to_7_Segment_decoder bcd_to_7_segment_decoder_4: pin names not known; wires that end beside it: G4, E4, F4, D4, counter_1_q, A4, C4, B4
  // BCD_to_7_Segment_decoder bcd_to_7_segment_decoder_5: pin names not known; wires that end beside it: G1, E1, F1, D1, {1'b0, counter_4_q}, A1, C1, B1
  _7_Segment_Display u_7_segment_display_1 (.g(G5), .f(F5), .a(A5), .b(B5), .e(E5), .d(D5), .c(C5));  // open: dp
  _7_Segment_Display u_7_segment_display_2 (.g(G4), .f(F4), .a(A4), .b(B4), .e(E4), .d(D4), .c(C4));  // open: dp
  // BCD_to_7_Segment_decoder bcd_to_7_segment_decoder_6: pin names not known; wires that end beside it: G5, E5, F5, D5, {1'b0, counter_2_q}, A5, C5, B5
  _7_Segment_Display u_7_segment_display_3 (.g(G3), .f(F3), .a(A3), .b(B3), .e(E3), .d(D3), .c(C3));  // open: dp
  _7_Segment_Display u_7_segment_display_4 (.g(G2), .f(F2), .a(A2), .b(B2), .e(E2), .d(D2), .c(C2));  // open: dp
  _7_Segment_Display u_7_segment_display_5 (.g(G1), .f(F1), .a(A1), .b(B1), .e(E1), .d(D1), .c(C1));  // open: dp
  _7_Segment_Display u_7_segment_display_6 (.g(G0), .f(F0), .a(A0), .b(B0), .e(E0), .d(D0), .c(C0));  // open: dp
  Counter #(.max('h3), .width(2)) counter_7 (
    .clr(1'b0), .count(1'b1), .clk(clock_1_out), .Q(counter_7_q));  // open: load, up, D, carry
  Decoder #(.select(2)) decoder_1 (
    .out0(decoder_1_out0), .out1(decoder_1_out1), .out2(decoder_1_out2), .out3(decoder_1_out3),
    .sel(counter_7_q));  // open: en
  _7_Segment_Display u_7_segment_display_7 ();  // open: g, f, a, b, e, d, c, dp
  // BCD_to_7_Segment_decoder bcd_to_7_segment_decoder_7: pin names not known; wires that end beside it: bcd_to_7_segment_decoder_7_p1
  _7_Segment_Display u_7_segment_display_8 ();  // open: g, f, a, b, e, d, c, dp
  // BCD_to_7_Segment_decoder bcd_to_7_segment_decoder_8: pin names not known; wires that end beside it: bcd_to_7_segment_decoder_8_p1
  Multiplexer #(.width(4)) multiplexer_1 (
    .in0(4'b1010), .in1({1'b0, counter_2_q}), .out(bcd_to_7_segment_decoder_7_p1), .sel(decoder_1_out3));
  Multiplexer #(.width(4)) multiplexer_2 (
    .in0(4'b1010), .in1(counter_1_q), .out(bcd_to_7_segment_decoder_8_p1), .sel(decoder_1_out2));
  _7_Segment_Display u_7_segment_display_9 ();  // open: g, f, a, b, e, d, c, dp
  // BCD_to_7_Segment_decoder bcd_to_7_segment_decoder_9: pin names not known; wires that end beside it: decoder_1_out1, bcd_to_7_segment_decoder_9_p2
  Multiplexer #(.width(4)) multiplexer_3 (
    .in0(4'b1010), .in1({1'b0, counter_6_q}), .out(bcd_to_7_segment_decoder_9_p2), .sel(decoder_1_out1));
  _7_Segment_Display u_7_segment_display_10 ();  // open: g, f, a, b, e, d, c, dp
  // BCD_to_7_Segment_decoder bcd_to_7_segment_decoder_10: pin names not known; wires that end beside it: bcd_to_7_segment_decoder_10_p1
  Multiplexer #(.width(4)) multiplexer_4 (
    .in0(4'b1010), .in1(counter_5_q), .out(bcd_to_7_segment_decoder_10_p1), .sel(decoder_1_out0));
endmodule
